// Logisim project mountain_of_arrows.circ as structural Verilog: 1 circuit, main circuit main
module main (
  input  BOUND_UP,
  input  PANIC,
  input  ENEMY_DOWN,
  output P_DOWN
);

  wire AND_GATE_1_out, AND_GATE_2_out, NOT_PANIC_out;

  not NOT_PANIC (NOT_PANIC_out, PANIC);
  and AND_GATE_1 (AND_GATE_1_out, BOUND_UP, NOT_PANIC_out);
  and AND_GATE_2 (AND_GATE_2_out, PANIC, ENEMY_DOWN);
  or OR_GATE (P_DOWN, AND_GATE_1_out, AND_GATE_2_out);
endmodule
